// Logisim project jaw280.circ as structural Verilog: 5 circuits, main circuit main
module main (
  input  in_1,
  input  in_2,
  input  [15:0] in_3
);

  wire clock_1_out;
  wire [3:0] display_unit_1_digit_1, display_unit_1_digit_2, display_unit_1_digit_3, display_unit_1_digit_4;

  Clock clock_1 (.out(clock_1_out));
  Hex_Digit_Display hex_digit_display_1 (.value(display_unit_1_digit_1));  // open: dp
  display_unit display_unit_1 (
    .Clock(clock_1_out), .Clear(in_1), .Write_Enable(in_2), .Data(in_3), .Digit_1(display_unit_1_digit_1),
    .Digit_2(display_unit_1_digit_2), .Digit_3(display_unit_1_digit_3), .Digit_4(display_unit_1_digit_4));
  Hex_Digit_Display hex_digit_display_2 (.value(display_unit_1_digit_3));  // open: dp
  Hex_Digit_Display hex_digit_display_3 (.value(display_unit_1_digit_2));  // open: dp
  Hex_Digit_Display hex_digit_display_4 (.value(display_unit_1_digit_4));  // open: dp
  ROM #(.addrWidth(16), .dataWidth(16)) rom_1 ();  // open: addr, data, sel
  RAM #(.addrWidth(16), .dataWidth(16), .bus("separate")) ram_1 ();  // open: addr, din, data, str, sel, clk, ld, clr
  alu alu_1 ();  // open: A, B, Operation, Result, High, Zero, Negative
  register_file register_file_1 ();  // open: Clock, Data, Write_Enable, rd, rs, rt, incr7, decr7, I_type, rs_out, rt_out
  Register #(.width(32)) product_register ();  // open: D, en, Q, clk, clr

  // Notes on the sheet:
  //   ROM
  //   contents of rom_1 (hex, n*v repeats v):
  //   8299 240 400
  //   RAM
endmodule

module display_unit (
  input  Clock,
  input  Clear,
  input  Write_Enable,
  input  [15:0] Data,
  output [3:0] Digit_1,
  output [3:0] Digit_2,
  output [3:0] Digit_3,
  output [3:0] Digit_4
);

  Register #(.width(16)) register_1 (
    .D(Data), .en(Write_Enable), .Q({Digit_1, Digit_2, Digit_3, Digit_4}), .clk(Clock), .clr(Clear));

  // Other names for the same wires on the sheet: clk = Clock; clr = Clear
endmodule

module alu (
  input  [15:0] A,
  input  [15:0] B,
  input  [2:0] Operation,
  output [15:0] Result,
  output [15:0] High,
  output Zero,
  output Negative
);

  wire [15:0] add_out, and_out, left_out, mult_out, not_out, or_out, right_out, sub_out;

  Adder #(.width(16)) adder_1 (.a(A), .b(B), .out(add_out));  // open: cin, cout
  assign and_out = A & B;  // AND_Gate and_1, 16 bits wide
  Shifter #(.width(16)) shifter_1 (.in(A), .\dist (B[3:0]), .out(left_out));
  Subtractor #(.width(16)) subtractor_1 (.a(A), .b(B), .out(sub_out));  // open: bin, bout
  assign or_out = A | A;  // OR_Gate or_1, 16 bits wide
  Multiplexer #(.select(3), .width(16), .enable("false")) multiplexer_1 (
    .in0(add_out), .in1(sub_out), .in2(mult_out), .in3(and_out), .in4(or_out), .in5(not_out), .in6(left_out),
    .in7(right_out), .out(Result), .sel(Operation));
  Multiplier #(.width(16)) multiplier_1 (.a(A), .b(B), .out(mult_out), .cout(High));  // open: cin
  Shifter #(.width(16), .shift("lr")) shifter_2 (.in(A), .\dist (B[3:0]), .out(right_out));
  assign not_out = ~A;  // NOT_Gate not_1, 16 bits wide
  Comparator #(.width(16)) comparator_1 (.a(Result), .b({16{1'b0}}), .eq(Zero));  // open: gt, lt
  Comparator #(.width(16)) comparator_2 (.a(Result), .b({16{1'b0}}), .lt(Negative));  // open: gt, eq

  // Other names for the same wires on the sheet: mult_high[15:0] = High; op[2:0] = Operation

  // Notes on the sheet:
  //   000 - add
  //   011 - and
  //   110 - shift left
  //   001 - sub
  //   100 - or
  //   010 - mult
  //   111 - shift right
  //   101 - not
endmodule

module register_file (
  input  Clock,
  input  [15:0] Data,
  input  Write_Enable,
  input  [2:0] rd,
  input  [2:0] rs,
  input  [2:0] rt,
  input  incr7,
  input  decr7,
  input  I_type,
  output [15:0] rs_out,
  output [15:0] rt_out
);

  wire demultiplexer_1_out7, r0en, r1en, r2en, r3en, r4en, r5en, r6en, r7en;
  wire [2:0] multiplexer_1_out;
  wire [15:0] adder_1_out, r0out, r1out, r2out, r3out, r4out, r5out, r6out, r7input, r7input2, r7out, r7out1,
       subtractor_1_out, subtractor_2_out;

  Multiplexer #(.width(3), .enable("false")) multiplexer_1 (.in0(rs), .in1(rd), .out(multiplexer_1_out), .sel(I_type));
  Multiplexer #(.select(3), .width(16), .enable("false")) multiplexer_2 (
    .in0(r0out), .in1(r1out), .in2(r2out), .in3(r3out), .in4(r4out), .in5(r5out), .in6(r6out), .in7(r7out),
    .out(rs_out), .sel(multiplexer_1_out));
  Register #(.width(16)) r0 (.D(Data), .en(r0en), .Q(r0out), .clk(Clock));  // open: clr
  Register #(.width(16)) r4 (.D(Data), .en(r4en), .Q(r4out), .clk(Clock));  // open: clr
  Multiplexer #(.select(3), .width(16), .enable("false")) multiplexer_3 (
    .in0(r0out), .in1(r1out), .in2(r2out), .in3(r3out), .in4(r4out), .in5(r5out), .in6(r6out), .in7(r7out),
    .out(rt_out), .sel(rt));
  Subtractor #(.width(16)) subtractor_1 (.a(r7out1), .b(16'h1), .out(subtractor_1_out));  // open: bin, bout
  Register #(.width(16)) r1 (.D(Data), .en(r1en), .Q(r1out), .clk(Clock));  // open: clr
  Register #(.width(16)) r5 (.D(Data), .en(r5en), .Q(r5out), .clk(Clock));  // open: clr
  Adder #(.width(16)) adder_1 (.a(r7out1), .b(16'h1), .out(adder_1_out));  // open: cin, cout
  Subtractor #(.width(16)) subtractor_2 (.a(r7out1), .b(16'h1), .out(subtractor_2_out));  // open: bin, bout
  Multiplexer #(.width(16), .enable("false")) multiplexer_4 (
    .in0(r7out1), .in1(subtractor_1_out), .out(r7out), .sel(decr7));
  Register #(.width(16)) r2 (.D(Data), .en(r2en), .Q(r2out), .clk(Clock));  // open: clr
  Register #(.width(16)) r6 (.D(Data), .en(r6en), .Q(r6out), .clk(Clock));  // open: clr
  Demultiplexer #(.select(3), .enable("false")) demultiplexer_1 (
    .out0(r0en), .out1(r1en), .out2(r2en), .out3(r3en), .out4(r4en), .out5(r5en), .out6(r6en),
    .out7(demultiplexer_1_out7), .in(Write_Enable), .sel(rd));
  Multiplexer #(.width(16), .enable("false")) multiplexer_5 (.in0(Data), .in1(adder_1_out), .out(r7input), .sel(incr7));
  Multiplexer #(.width(16), .enable("false")) multiplexer_6 (
    .in0(r7input), .in1(subtractor_2_out), .out(r7input2), .sel(decr7));
  // Probe on r7input2
  Register #(.width(16)) r3 (.D(Data), .en(r3en), .Q(r3out), .clk(Clock));  // open: clr
  Register #(.width(16)) r7 (.D(r7input2), .en(r7en), .Q(r7out1), .clk(Clock));  // open: clr
  or or_1 (r7en, incr7, demultiplexer_1_out7, decr7);

  // Other names for the same wires on the sheet: CLK = Clock; ITYPE = I_type; RSOUT[15:0] = rs_out;
  //   RTOUT[15:0] = rt_out; WRE = Write_Enable
endmodule

module program_counter_control (
  input  Halt,
  input  [7:0] Immediate,
  input  in_3
);

  wire [15:0] pc_in, pc_next, pc_out;

  Adder #(.width(16)) adder_1 (.a(pc_out), .b(16'h1), .out(pc_next));  // open: cin, cout
  Register #(.width(16)) register_1 (.D(pc_in), .en(Halt), .Q(pc_out));  // open: clk, clr
  Multiplexer #(.select(3)) multiplexer_1 ();  // open: in0, in1, in2, in3, in4, in5, in6, in7, out, sel, en

  // Other names for the same wires on the sheet: imm[7:0] = Immediate
endmodule
